# Fritzing sketch DHT11 (saved by Fritzing 0.8.5b)
circuit board: 8.46667cm x 5.64444cm
breadboards: 1

parts:
  Ground = Pad [width=3.73994049918257 height=2.98159945673017 connect=center]  # not connected
  Vcc = Pad [width=7.38080952151676 height=4.34825761560847 connect=center]  # not connected
  Raspberry_Pi_out = Pad [width=4.78483012339685 height=3.90853076808732 connect=center]  # not connected
  Raspberry_Pi_B_rev1 = Raspberry Pi B rev1
  DHT1 = DHT11 Humitidy and Temperature Sensor
  R1 = Resistor [package="2010 [SMD]"]

nets (from the breadboard view):
  5V: Raspberry_Pi_B_rev1.5V, Raspberry_Pi_B_rev1.GPIO_23, Raspberry_Pi_B_rev1.GPIO_22, DHT1.VDD, R1.Pin_1
  GND: Raspberry_Pi_B_rev1.GND, Raspberry_Pi_B_rev1.GPIO_21, Raspberry_Pi_B_rev1.GPIO_9, Raspberry_Pi_B_rev1.GPIO_11, DHT1.GND
  N1: Raspberry_Pi_B_rev1.GPIO_4, DHT1.DATA, R1.Pin_0
  N2: Raspberry_Pi_B_rev1.GPIO_25, Raspberry_Pi_B_rev1.GPIO_8, Raspberry_Pi_B_rev1.GPIO_7

notes:
  DHT 11 Humidity & Temperature Sensor

custom parts:
  DHT11 Humitidy and Temperature Sensor: DHT11 Humidity and Temperature Sensor
